# Fritzing sketch BME 280 (saved by Fritzing 0.9.3b)
breadboards: 1

parts:
  Part1 = Arduino Ethernet Shield (Rev3)
  Part2 = BME280 Breakout  # not connected
  U1 = LCD-16X2 [package=lcd-16x2]
  R3 = Rotary Potentiometer (Large) [maximum_resistance=100kΩ package=THT]
  R4 = Resistor [tolerance=±5% resistance=220 package="2010 [SMD]"]
  LED1 = smd LED [color="Red (633nm)" package="0603 [SMD]"]
  R5 = Photocell (LDR) [package=THT]
  R6 = Resistor [tolerance=±5% resistance=220 package="2010 [SMD]"]

nets:
  N1: Part1.D8, U1.RS
  N2: Part1.PWM_D9, U1.E
  N3: Part1.A0, R5.pin_1, R6.Pin_0
  N4: Part1.D2, LED1.cathode
  N5: Part1.PWM_D3, U1.DB4
  N6: Part1.PWM_D5, U1.DB5
  N7: Part1.PWM_D6, U1.DB6
  N8: Part1.D7, U1.DB7
  N9: Part1.3V3, R5.pin_0
  5V: Part1.5V, U1.VDD, U1.A, R3.leg2, R4.Pin_0
  GND: Part1.GND, U1.VSS, U1.R_W, U1.K, R3.leg1, R6.Pin_1
  N10: U1.VO, R3.wiper
  N11: R4.Pin_1, LED1.anode
